// Logisim project 2sComplimentWithDecoder.circ as structural Verilog: 1 circuit, main circuit main
module main (
  input  Enable,
  input  [3:0] in_2,
  output MSB,
  output out_4,
  output out_5,
  output LSB
);

  wire decoder_1_out0, decoder_1_out1, decoder_1_out2, decoder_1_out3, decoder_1_out4, decoder_1_out5,
       decoder_1_out6, decoder_1_out7, decoder_1_out8, decoder_1_out9, decoder_1_out10, decoder_1_out11,
       decoder_1_out12, decoder_1_out13, decoder_1_out14, decoder_1_out15;

  Decoder #(.select(4)) decoder_1 (
    .out0(decoder_1_out0), .out1(decoder_1_out1), .out2(decoder_1_out2), .out3(decoder_1_out3),
    .out4(decoder_1_out4), .out5(decoder_1_out5), .out6(decoder_1_out6), .out7(decoder_1_out7),
    .out8(decoder_1_out8), .out9(decoder_1_out9), .out10(decoder_1_out10), .out11(decoder_1_out11),
    .out12(decoder_1_out12), .out13(decoder_1_out13), .out14(decoder_1_out14), .out15(decoder_1_out15),
    .sel(in_2), .en(Enable));
  or or_1 (MSB, decoder_1_out1, decoder_1_out2, decoder_1_out3, decoder_1_out4, decoder_1_out5, decoder_1_out6, decoder_1_out7, decoder_1_out8);
  or or_2 (out_4, decoder_1_out1, decoder_1_out2, decoder_1_out3, decoder_1_out4, decoder_1_out9, decoder_1_out10, decoder_1_out11, decoder_1_out12);
  or or_3 (out_5, decoder_1_out1, decoder_1_out2, decoder_1_out5, decoder_1_out6, decoder_1_out9, decoder_1_out10, decoder_1_out13, decoder_1_out14);
  or or_4 (LSB, decoder_1_out1, decoder_1_out3, decoder_1_out5, decoder_1_out7, decoder_1_out9, decoder_1_out11, decoder_1_out13, decoder_1_out15);
endmodule
