// Logisim project AdderWithMultiPlexer.circ as structural Verilog: 1 circuit, main circuit main
module main (
  input  C,
  input  [1:0] X___Y,
  output Sum,
  output Carry
);

  wire not_1_out;

  not not_1 (not_1_out, C);
  Multiplexer #(.select(2), .enable("false")) multiplexer_1 (
    .in0(C), .in1(not_1_out), .in2(not_1_out), .in3(C), .out(Sum), .sel(X___Y));
  Multiplexer #(.select(2), .enable("false")) multiplexer_2 (
    .in0(1'b0), .in1(C), .in2(C), .in3(1'b1), .out(Carry), .sel(X___Y));
endmodule
