// Logisim project GrayToBinaryCircuit.circ as structural Verilog: 1 circuit, main circuit main
module main (
  input  A,
  input  B,
  input  C,
  input  D,
  output w,
  output x,
  output y,
  output z
);

  wire not_1_out, not_2_out, not_3_out, not_4_out;

  not not_1 (not_1_out, A);
  not not_2 (not_2_out, B);
  not not_3 (not_3_out, D);
  not not_4 (not_4_out, C);
  xor xor_1 (x, A, B);
  xor xor_2 (y, x, C);
  xor xor_3 (z, y, D);

  assign w = A;

  // Notes on the sheet:
  //   Gray code -> Binary Number
endmodule
