// Logisim project GrayToBinaryGeneralised.circ as structural Verilog: 1 circuit, main circuit main
module main (
  input  A,
  input  B,
  input  C,
  input  D,
  input  E,
  output w,
  output x,
  output y,
  output z,
  output out_10
);

  xor xor_1 (x, A, B);
  xor xor_2 (y, x, C);
  xor xor_3 (z, y, D);
  xor xor_4 (out_10, z, E);

  assign w = A;

  // Notes on the sheet:
  //   Gray code -> Binary Number
  //   Generalised
endmodule
