// Logisim project Problem2.circ as structural Verilog: 1 circuit, main circuit main
module main (
  input  C,
  input  [1:0] A_B,
  input  [2:0] A_B_C,
  output F,
  output F_2
);

  wire decoder_1_out3, decoder_1_out4, decoder_1_out5, decoder_1_out7;

  Multiplexer #(.select(2), .enable("false")) multiplexer_1 (
    .in0(1'b0), .in1(C), .in2(1'b1), .in3(C), .out(F), .sel(A_B));
  Decoder #(.select(3), .enable("false")) decoder_1 (
    .out3(decoder_1_out3), .out4(decoder_1_out4), .out5(decoder_1_out5), .out7(decoder_1_out7), .sel(A_B_C));  // open: out0, out1, out2, out6
  or or_1 (F_2, decoder_1_out3, decoder_1_out4, decoder_1_out5, decoder_1_out7);

  // Notes on the sheet:
  //   IMPLEMENTATION OF AB' + BC
endmodule
