// Logisim project Problem3.circ as structural Verilog: 1 circuit, main circuit main
module main (
  input  A,
  input  B,
  input  C,
  input  D,
  output out_5,
  output out_6,
  output out_7,
  output out_8,
  output Error
);

  wire and_2_out, and_3_out, not_1_out, not_2_out, not_3_out;

  not not_1 (not_1_out, A);
  not not_2 (not_2_out, B);
  not not_3 (not_3_out, C);
  not not_4 (out_8, D);
  xor xor_1 (out_6, C, B);
  and and_1 (out_5, not_1_out, not_2_out, not_3_out);
  and and_2 (and_2_out, A, C);
  and and_3 (and_3_out, A, B);
  or or_1 (Error, and_2_out, and_3_out);

  assign out_7 = C;
endmodule
