// Logisim project Problem4.circ as structural Verilog: 1 circuit, main circuit main
module main (
  input  C,
  input  [1:0] A_B,
  input  [2:0] A_B_C,
  output out_4,
  output out_5
);

  wire decoder_1_out3, decoder_1_out5, decoder_1_out6, decoder_1_out7;

  Multiplexer #(.select(2), .enable("false")) multiplexer_1 (
    .in0(1'b0), .in1(C), .in2(C), .in3(1'b1), .out(out_4), .sel(A_B));
  Decoder #(.select(3), .enable("false")) decoder_1 (
    .out3(decoder_1_out3), .out5(decoder_1_out5), .out6(decoder_1_out6), .out7(decoder_1_out7), .sel(A_B_C));  // open: out0, out1, out2, out4
  or or_1 (out_5, decoder_1_out3, decoder_1_out5, decoder_1_out6, decoder_1_out7);
endmodule
