// Logisim project Double_BCD_To_7SegDisplay.circ as structural Verilog: 1 circuit, main circuit main
module main (
  input  MSB,
  input  in_2,
  input  in_3,
  input  in_4,
  input  MSB_2,
  input  in_6,
  input  in_7,
  input  in_8
);

  wire n7_segment_1_a_2, n7_segment_1_b_2, n7_segment_1_c_2, n7_segment_1_d_2, n7_segment_1_e,
       n7_segment_1_f, n7_segment_1_g, n7_segment_2_a_2, n7_segment_2_b_2, n7_segment_2_c_2,
       n7_segment_2_d_2, n7_segment_2_e, n7_segment_2_f, n7_segment_2_g;

  _7_Segment u_7_segment_1 (
    .A(MSB), .B(in_2), .C(in_3), .D(in_4), .a_2(n7_segment_1_a_2), .b_2(n7_segment_1_b_2),
    .c_2(n7_segment_1_c_2), .d_2(n7_segment_1_d_2), .e(n7_segment_1_e), .f(n7_segment_1_f), .g(n7_segment_1_g));
  _7_Segment u_7_segment_2 (
    .A(MSB_2), .B(in_6), .C(in_7), .D(in_8), .a_2(n7_segment_2_a_2), .b_2(n7_segment_2_b_2),
    .c_2(n7_segment_2_c_2), .d_2(n7_segment_2_d_2), .e(n7_segment_2_e), .f(n7_segment_2_f), .g(n7_segment_2_g));
  _7_Segment_Display u_7_segment_display_1 (
    .g(n7_segment_1_g), .f(n7_segment_1_f), .a(n7_segment_1_a_2), .b(n7_segment_1_b_2), .e(n7_segment_1_e),
    .d(n7_segment_1_d_2), .c(n7_segment_1_c_2));  // open: dp
  _7_Segment_Display u_7_segment_display_2 (
    .g(n7_segment_2_g), .f(n7_segment_2_f), .a(n7_segment_2_a_2), .b(n7_segment_2_b_2), .e(n7_segment_2_e),
    .d(n7_segment_2_d_2), .c(n7_segment_2_c_2));  // open: dp
endmodule
