// Logisim project Lab1.circ as structural Verilog: 2 circuits, main circuit main
module main (
  input  in_1,
  input  in_2,
  input  in_3,
  input  in_4
);

  wire n7_segment_1_a_2, n7_segment_1_b_2, n7_segment_1_c_2, n7_segment_1_d_2, n7_segment_1_e,
       n7_segment_1_f, n7_segment_1_g;

  _7_Segment u_7_segment_1 (
    .A(in_1), .B(in_2), .C(in_3), .D(in_4), .a_2(n7_segment_1_a_2), .b_2(n7_segment_1_b_2),
    .c_2(n7_segment_1_c_2), .d_2(n7_segment_1_d_2), .e(n7_segment_1_e), .f(n7_segment_1_f), .g(n7_segment_1_g));
  _7_Segment_Display u_7_segment_display_1 (
    .g(n7_segment_1_g), .f(n7_segment_1_f), .a(n7_segment_1_a_2), .b(n7_segment_1_b_2), .e(n7_segment_1_e),
    .d(n7_segment_1_d_2), .c(n7_segment_1_c_2));  // open: dp

  // Notes on the sheet:
  //   a
  //   A
  //   b
  //   c
  //   B
  //   d
  //   C
  //   e
  //   D
  //   f
  //   g
endmodule

module _7_Segment (
  input  A,
  input  B,
  input  C,
  input  D,
  output a_2,
  output b_2,
  output c_2,
  output d_2,
  output e,
  output f,
  output g
);

  wire nand_1_out, nand_2_out, nand_3_out, nand_4_out, nand_5_out, nand_6_out, nand_7_out, nand_8_out,
       nand_9_out, nand_10_out, nand_11_out, nand_12_out, nand_13_out, nand_14_out, nand_15_out, nand_16_out,
       nand_17_out, nand_18_out, nand_19_out, nand_20_out, nand_21_out, nand_22_out, nand_23_out,
       nand_24_out, nand_25_out, nand_26_out, nand_27_out, nand_29_out, nand_30_out, nand_31_out,
       nand_32_out, nand_33_out, nand_34_out, nand_35_out, nand_36_out, nand_37_out, nand_38_out,
       nand_39_out, nand_40_out, nand_41_out, nand_42_out, nand_43_out;

  nand nand_1 (nand_1_out, B, B);
  nand nand_2 (nand_2_out, D, D);
  nand nand_3 (nand_3_out, C, C);
  nand nand_4 (nand_4_out, D, D);
  nand nand_5 (nand_5_out, D, D);
  nand nand_6 (nand_6_out, B, B);
  nand nand_7 (nand_7_out, B, B);
  nand nand_8 (nand_8_out, D, D);
  nand nand_9 (nand_9_out, B, B);
  nand nand_10 (nand_10_out, D, D);
  nand nand_11 (nand_11_out, C, C);
  nand nand_12 (nand_12_out, B, B);
  nand nand_13 (nand_13_out, D, D);
  nand nand_14 (nand_14_out, D, D);
  nand nand_15 (nand_15_out, C, C);
  nand nand_16 (nand_16_out, D, D);
  nand nand_17 (nand_17_out, C, C);
  nand nand_18 (nand_18_out, D, D);
  nand nand_19 (nand_19_out, B, B);
  nand nand_20 (nand_20_out, C, C);
  nand nand_21 (nand_21_out, D, D);
  nand nand_22 (nand_22_out, nand_1_out, nand_2_out);
  nand nand_23 (nand_23_out, C, C);
  nand nand_24 (nand_24_out, B, D);
  nand nand_25 (nand_25_out, A, A);
  nand nand_26 (nand_26_out, nand_3_out, nand_4_out);
  nand nand_27 (nand_27_out, C, D);
  nand nand_28 (c_2, C, nand_5_out, nand_6_out);
  nand nand_29 (nand_29_out, nand_7_out, nand_8_out);
  nand nand_30 (nand_30_out, nand_9_out, C);
  nand nand_31 (nand_31_out, C, nand_10_out);
  nand nand_32 (nand_32_out, B, nand_11_out, D);
  nand nand_33 (nand_33_out, A, A);
  nand nand_34 (nand_34_out, nand_12_out, nand_13_out);
  nand nand_35 (nand_35_out, C, nand_14_out);
  nand nand_36 (nand_36_out, nand_15_out, nand_16_out);
  nand nand_37 (nand_37_out, B, nand_17_out);
  nand nand_38 (nand_38_out, B, nand_18_out);
  nand nand_39 (nand_39_out, A, A);
  nand nand_40 (nand_40_out, nand_19_out, C);
  nand nand_41 (nand_41_out, B, nand_20_out);
  nand nand_42 (nand_42_out, B, nand_21_out);
  nand nand_43 (nand_43_out, A, A);
  nand nand_44 (a_2, nand_22_out, nand_23_out, nand_24_out, nand_25_out);
  nand nand_45 (b_2, B, nand_26_out, nand_27_out);
  nand nand_46 (d_2, nand_29_out, nand_30_out, nand_31_out, nand_32_out, nand_33_out);
  nand nand_47 (e, nand_34_out, nand_35_out);
  nand nand_48 (f, nand_36_out, nand_37_out, nand_38_out, nand_39_out);
  nand nand_49 (g, nand_40_out, nand_41_out, nand_42_out, nand_43_out);
endmodule
