// Logisim project Problem1Circuit.circ as structural Verilog: 1 circuit, main circuit main
module main (
  input  x,
  input  y,
  output out_3
);

  wire nand_1_out, nand_2_out, nand_3_out;

  nand nand_1 (nand_1_out, x, y);
  nand nand_2 (nand_2_out, x, nand_1_out);
  nand nand_3 (nand_3_out, nand_1_out, y);
  nand nand_4 (out_3, nand_2_out, nand_3_out);
endmodule
