// Logisim project Problem2Circuit.circ as structural Verilog: 1 circuit, main circuit main
module main (
  input  a_prime,
  input  b_prime,
  input  c_prime,
  input  a_prime_2,
  input  b_prime_2,
  input  c_prime_2,
  input  a_prime_3,
  input  b_prime_3,
  input  c_prime_3,
  input  a_prime_4,
  input  b_prime_4,
  input  c_prime_4,
  input  a_prime_5,
  input  b_prime_5,
  input  c_prime_5,
  output out_16,
  output out_17,
  output out_18,
  output out_19,
  output out_20
);

  wire and_1_out, and_2_out, and_3_out, and_4_out, and_5_out, and_6_out, and_7_out, nand_1_out, nand_2_out,
       nand_3_out, nor_1_out, nor_2_out, nor_3_out, nor_4_out, not_1_out, not_2_out, not_3_out, not_4_out,
       not_5_out, not_6_out, not_7_out, not_8_out, not_9_out, not_10_out, not_11_out, not_12_out, not_15_out,
       not_16_out, not_17_out, not_18_out, not_19_out, not_20_out, not_21_out, not_22_out, not_23_out,
       or_2_out, or_3_out, or_4_out;

  not not_1 (not_1_out, a_prime);
  not not_2 (not_2_out, b_prime);
  not not_3 (not_3_out, a_prime_3);
  not not_4 (not_4_out, b_prime_3);
  not not_5 (not_5_out, b_prime_5);
  not not_6 (not_6_out, a_prime_5);
  not not_7 (not_7_out, c_prime);
  not not_8 (not_8_out, c_prime_3);
  not not_9 (not_9_out, c_prime_5);
  and and_1 (and_1_out, not_3_out, b_prime_3);
  and and_2 (and_2_out, a_prime_3, not_4_out);
  and and_3 (and_3_out, b_prime_3, not_8_out);
  nor nor_1 (nor_1_out, a_prime_5, not_5_out);
  nor nor_2 (nor_2_out, not_6_out, b_prime_5);
  nor nor_3 (nor_3_out, not_5_out, c_prime_5);
  and and_4 (and_4_out, not_1_out, b_prime);
  and and_5 (and_5_out, a_prime, not_2_out);
  and and_6 (and_6_out, b_prime, not_7_out);
  not not_10 (not_10_out, and_1_out);
  not not_11 (not_11_out, and_2_out);
  not not_12 (not_12_out, and_3_out);
  or or_1 (out_16, and_4_out, and_5_out, and_6_out);
  not not_13 (out_18, and_7_out);
  and and_7 (and_7_out, not_10_out, not_11_out, not_12_out);
  not not_14 (out_20, nor_4_out);
  nor nor_4 (nor_4_out, nor_1_out, nor_2_out, nor_3_out);
  not not_15 (not_15_out, a_prime_2);
  not not_16 (not_16_out, a_prime_4);
  not not_17 (not_17_out, c_prime_2);
  not not_18 (not_18_out, b_prime_2);
  not not_19 (not_19_out, b_prime_4);
  not not_20 (not_20_out, c_prime_4);
  or or_2 (or_2_out, a_prime_2, not_18_out);
  not not_21 (not_21_out, or_2_out);
  not not_22 (not_22_out, or_3_out);
  or or_3 (or_3_out, not_15_out, b_prime_2);
  not not_23 (not_23_out, or_4_out);
  or or_4 (or_4_out, not_18_out, c_prime_2);
  nand nand_1 (nand_1_out, not_16_out, b_prime_4);
  nand nand_2 (nand_2_out, a_prime_4, not_19_out);
  nand nand_3 (nand_3_out, b_prime_4, not_20_out);
  or or_5 (out_17, not_21_out, not_22_out, not_23_out);
  nand nand_4 (out_19, nand_1_out, nand_2_out, nand_3_out);

  // Notes on the sheet:
  //   a
  //   a
  //   a
  //   AND | OR | INVERTERS
  //   b
  //   AND | INVERTERS
  //   b
  //   NOR | INVERTERS
  //   b
  //   c
  //   c
  //   c
  //   a
  //   a
  //   OR | INVERTERS
  //   c
  //   b
  //   NAND | INVERTERS
  //   c
  //   b
endmodule
