// Logisim project Problem3Circuit.circ as structural Verilog: 1 circuit, main circuit main
module main (
  input  a,
  input  b,
  input  c,
  output X,
  output Y
);

  wire and_1_out, not_1_out, not_2_out, not_3_out, or_1_out, or_2_out;

  not not_1 (not_1_out, b);
  not not_2 (not_2_out, c);
  not not_3 (not_3_out, a);
  or or_1 (or_1_out, a, not_1_out);
  and and_1 (and_1_out, not_3_out, b);
  and and_2 (X, or_1_out, not_2_out);
  or or_2 (or_2_out, and_1_out, c);
  not not_4 (Y, or_2_out);
endmodule
