// Logisim project firstCircuit.circ as structural Verilog: 1 circuit, main circuit main
module main (
  input  A,
  input  A_2,
  input  B,
  input  B_2,
  input  A_3,
  input  A_4,
  input  B_3,
  input  B_4,
  input  A_5,
  input  A_6,
  input  B_5,
  input  B_6,
  input  A_7,
  input  A_8,
  output out_15,
  output out_16,
  output out_17,
  output out_18,
  output out_19,
  output out_20,
  output out_21,
  output out_22
);

  and and_1 (out_15, A, B);
  or or_1 (out_17, A_3, B_3);
  nand nand_1 (out_19, A_5, B_5);
  not not_1 (out_21, A_7);
  buf buffer_1 (out_22, A_8);
  nor nor_1 (out_16, A_2, B_2);
  xor xor_1 (out_18, A_4, B_4);
  xnor xnor_1 (out_20, A_6, B_6);
endmodule
