// Logisim project invertorsNANDandNOR.circ as structural Verilog: 1 circuit, main circuit main
module main (
  input  A,
  input  A_2,
  output A_prime,
  output A_prime_2
);

  nand nand_1 (A_prime, A, A);
  nor nor_1 (A_prime_2, A_2, A_2);
endmodule
