// Logisim project secondCircuit.circ as structural Verilog: 1 circuit, main circuit main
module main (
  input  a,
  input  b,
  input  c,
  input  d,
  input  e,
  input  f,
  output y1,
  output y2
);

  wire nand_1_out, not_1_out, or_1_out;

  not not_1 (not_1_out, b);
  or or_1 (or_1_out, c, d, e);
  xor xor_1 (y1, a, or_1_out);
  nand nand_1 (nand_1_out, not_1_out, or_1_out, f);
  not not_2 (y2, nand_1_out);
endmodule
