// Logisim project thirdCircuit.circ as structural Verilog: 1 circuit, main circuit main
module main (
  input  D0,
  input  D1,
  input  D2,
  input  D3,
  input  Control,
  output Q0,
  output Q1,
  output Q2,
  output Q3
);

  wire or_1_out, or_2_out, or_3_out;

  or or_1 (or_1_out, D1, or_2_out);
  or or_2 (or_2_out, D2, or_3_out);
  or or_3 (or_3_out, D3, Control);
  xor xor_1 (Q0, D0, or_1_out);
  xor xor_2 (Q1, D1, or_2_out);
  xor xor_3 (Q2, D2, or_3_out);
  xor xor_4 (Q3, D3, Control);
endmodule
